# Fritzing sketch circuito (saved by Fritzing 1.0.1rc)
breadboards: 1

parts:
  L298N2 = L298N DC motor driver
  Componente1 = Arduino Uno (Rev3)
  Mod1 = flyskyr6b
  M2 = DC Motor [voltage_(max)=6V voltage_(min)=3V]  # not connected
  M3 = DC Motor [voltage_(max)=6V voltage_(min)=3V]  # not connected
  WATER_PUMP1 = water pump/motor  # not connected
  U3 = TRANSCHIPTC5747 [package=camera_sfv24r-2st_2]
  R2 = Resistor [tolerance=±5% resistance=220 package="1206 [SMD]"]
  LED1 = LED - 5mm [color="Red (633nm)" current=0.030 package="5 mm [THT]"]
  LED2 = LED - 5mm [color="Blue (470nm)" current=0.030 package="5 mm [THT]"]
  R1 = Resistor [tolerance=±5% resistance=220 package="1206 [SMD]"]
  Q1 = TRANSISTOR_NPN [package=to-92]
  J1 = Piezo Speaker
  VCC1 = Battery block 9V  # not connected

nets:
  N1: L298N2.GND, U3.DVDD28, LED1.cathode, LED2.cathode, J1.pin1
  5V: L298N2.5V, Componente1.VIN, Mod1.VCC, Mod1.BAT+, U3.SDIN, Q1.E
  N2: L298N2.ENA, Componente1.D11_PWM/MOSI
  N3: L298N2.ENB, Componente1.D10_PWM/SS
  N4: L298N2.IN1, Componente1.A0
  N5: L298N2.IN2, Componente1.A1
  N6: L298N2.IN3, Componente1.A2
  N7: L298N2.IN4, Componente1.A3
  N8: Componente1.D8, Q1.B
  N9: Componente1.D9_PWM, R2.Pin_0
  N10: Componente1.D3_PWM, Mod1.CH1
  N11: Componente1.D5_PWM, Mod1.CH3
  N12: Componente1.D6_PWM, Mod1.CH5
  N13: Componente1.D7, R1.Pin_0
  GND: Componente1.GND, Mod1.connector14, Mod1.GND

notes:
  7.4V
  (our battery)
  (FPV camera + FPV transmitter)
  Water pump
  Buzzer
  Motor Controller
  L298N
  FlySky FS-IA6
  Transistor BC547
  Geared Motor Right
  Geared Motor Left

custom parts:
  L298N DC motor driver: 2x DC motor driver with 78M05 positive voltage regulator (7..35 V) L298N: max 46 V, 2 A Set 5 V Enable jumper to enable 5 V regultor (needed for the L298N) and +5 V output at screw terminal or supply external +5 V at screw terminal Set ENA and/or ENB to +5 V to enable motor permanently or supply ENA and/or ENB with PWM signal IN1 and IN2 set rotation directory for motor A (OUT1/OUT2) IN2 and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
  flyskyr6b: flysky r6b 6ch rc receiver module. Pcb view is 3*7 header pins, 3 female headers will let the board plug in to the receiver, or connect via wires as you choose.
  water pump/motor: WATER PUMP BY ARDUBLOCKTR
  Battery block 9V: 9 Volt battery block with 200mil pcb footprint spacing
